# Fritzing sketch Proxima_R2CV (saved by Fritzing 1.0.5)
breadboards: 1

parts:
  Mod1 = Raspberry Pi Pico
  Bauteil1 = Adafruit MCP4725 Breakout Board - 12-Bit DAC [part_number="Adafruit #935"]
  VL53L0X1 = VL53L0X ToF laser distance sensor [package=THT]
  U1 = LM 358 Dual Op-Amp [package="SO 08 [SMD]"]  # not connected
  R1 = 10k Ω Resistor [package=THT]
  C1 = Ceramic Capacitor [capacitance=100nF voltage=35V package="200 mil [THT, multilayer]"]
  R2 = 10k Ω Resistor [package=THT]
  R3 = 10k Ω Resistor [package=THT]

nets:
  GND: Mod1.pin_3, Mod1.pin_8, Mod1.pin_13, Mod1.pin_18, Mod1.pin_23, Mod1.pin_28, Mod1.pin_33, Mod1.pin_38, Bauteil1.GND, VL53L0X1.GND, C1.1, R2.Pin_1
  N1: Mod1.pin_6, Bauteil1.SDA, VL53L0X1.SDA
  N2: Mod1.pin_7, Bauteil1.SCL, VL53L0X1.SCL
  VDD: Mod1.pin_36, Bauteil1.VDD, VL53L0X1.VIN
  N3: Bauteil1.VOUT, R1.Pin_0
  N4: VL53L0X1.X, VL53L0X1.G
  N5: R1.Pin_1, C1.0
  N6: R2.Pin_0, R3.Pin_1

custom parts:
  Raspberry Pi Pico: Raspberry Pi Pico. Based around the RP2040 microcontroller the Pico is a low cost microcontroller device bringing Raspberry Pi quality, cost, and easy of use to the microcontroller space. Jan 2021, Split part in to two versions: tht (this one) and SMD. This one will drill holes for a .1 in header in pcb to allow plugging in the module as well as providing pads to solder the module to the top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
  Adafruit MCP4725 Breakout Board - 12-Bit DAC: Your microcontroller probably has an ADC (analog -> digital converter) but does it have a DAC (digital -> analog converter)??? Now it can! This breakout board features the easy-to-use MCP4725 12-bit DAC. Control it via I2C and send it the value you want it to output, and the VOUT pin will have it. Great for audio / analog projects, such as when you can't use PWM but need a sine wave or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
  VL53L0X ToF laser distance sensor: Time of Flight laser distance sensor VL53L0X.
  10k Ω Resistor: A generic resistor (0.25W)
